# Fritzing sketch rgb-photon (saved by Fritzing 0.9.3b)
circuit board: 8.46667cm x 5.64444cm
breadboards: 1

parts:
  Part1 = Photon
  R1 = Resistor [tolerance=±5% resistance=220 package=THT]
  R2 = Resistor [tolerance=±5% resistance=100 package=THT]
  R3 = Resistor [tolerance=±5% resistance=100 package=THT]
  LED1 = RGB LED - (4 legs) [package="5 mm [THT]"]

nets:
  N1: Part1.GND, LED1.common_anode
  N2: Part1.D0, R1.Pin_0
  N3: Part1.D1, R3.Pin_0
  N4: Part1.D2, R2.Pin_0
  N5: R1.Pin_1, LED1.red_cathode
  N6: R2.Pin_1, LED1.blue_cathode
  N7: R3.Pin_1, LED1.green_cathode
